# Fritzing sketch circuit_diagram (saved by Fritzing 0.9.3b)
perfboards: 1

parts:
  Arduino_Nano = Arduino Nano (Rev3.0)
  Stromversorgung_Schienenabgreifer = 2.1mm Barrel Jack with Terminal Block
  TL7805 = Voltage Regulator [package=to-220-alt]
  R3 = Resistor [tolerance=±5% resistance=1k package="0603 [SMD]"]
  R4 = Resistor [tolerance=±5% resistance=10k package="0603 [SMD]"]
  IC3 = IC, DIP package, 26 pins [chip_label=Sockelleiste]
  MOSFET_IRF9640 = Basic FET P-Channel [package="DPak [SMD]"]
  NPN-Transistor_P2N2222A = NPN-Transistor [package="SOT-23 [SMD]"]
  Diode = Rectifier Diode [package="Melf DO-213 AA [SMD]"]
  Motor = DC Motor
  LED1 = smd LED [color="Green (555nm)" package="0603 [SMD]"]
  LED2 = smd LED [color="Red (633nm)" package="0603 [SMD]"]
  C1 = Electrolytic Capacitor [capacitance=100μF package="0807 [SMD, electrolytic]"]
  C2 = Electrolytic Capacitor [package="200 mil [THT, electrolytic]"]
  Bridge_Rectifier = IC, DIP package, 4 pins [chip_label=BridgeRect]
  Gyro_MPU6050 = MPU-6050 Board GY-521 [form="♀ (female)" package=THT]
  Diode_(4004) = Rectifier Diode [package="Melf DO-213 AA [SMD]"]
  Diode_(4004)_2 = Rectifier Diode [package="Melf DO-213 AA [SMD]"]
  Bauteil1 = Adafruit VL53L0X Time of Flight Distance Sensor [part_number="Adafruit #3317"]

nets:
  GND: Arduino_Nano.GND, IC3.pin24, LED1.cathode, LED2.cathode, Gyro_MPU6050.pin2, Bauteil1.GND
  N1: Arduino_Nano.D2, Gyro_MPU6050.pin8
  N2: Arduino_Nano.D4, LED2.anode
  N3: Arduino_Nano.D5, LED1.anode
  N4: Arduino_Nano.D9, IC3.pin18
  VIN: Arduino_Nano.VIN, IC3.pin23, Bauteil1.VIN
  N5: Arduino_Nano.5V, Gyro_MPU6050.pin1
  N6: Arduino_Nano.A5, Gyro_MPU6050.pin3, Bauteil1.SCL
  N7: Arduino_Nano.A4, Gyro_MPU6050.pin4, Bauteil1.SDA
  N8: Stromversorgung_Schienenabgreifer.POS, IC3.pin26
  N9: Stromversorgung_Schienenabgreifer.NEG, IC3.pin25
  N10: TL7805.GND, IC3.pin3, IC3.pin7, IC3.pin12, MOSFET_IRF9640.drain, NPN-Transistor_P2N2222A.1, C1.-, C2.-, Bridge_Rectifier.pin3
  N11: TL7805.OUT, IC3.pin4, C1.+, C2.+
  N12: R3.Pin_0, NPN-Transistor_P2N2222A.0
  N13: R3.Pin_1, IC3.pin9
  N14: R4.Pin_0, IC3.pin8, IC3.pin11, IC3.pin13, Diode.cathode, Motor.pin_1, Diode_(4004).cathode
  N15: R4.Pin_1, MOSFET_IRF9640.Gate, NPN-Transistor_P2N2222A.2
  N16: IC3.pin1, Bridge_Rectifier.pin2
  N17: IC3.pin2, Bridge_Rectifier.pin1
  N18: IC3.pin10, MOSFET_IRF9640.source, Diode.anode, Motor.pin_2
  N19: Bridge_Rectifier.pin4, Diode_(4004).anode, Diode_(4004)_2.anode

custom parts:
  Electrolytic Capacitor: electrolytic capacitor
  MPU-6050 Board GY-521: Acelerometro y Giroscopio MPU-6050 Board GY-521
  Adafruit VL53L0X Time of Flight Distance Sensor: The VL53L0X is a Time of Flight distance sensor like no other you've used! The sensor contains a very tiny invisible laser source, and a matching sensor. The VL53L0X can detect the "time of flight", or how long the light has taken to bounce back to the sensor. Since it uses a very narrow light source, it is good for determining distance of only the surface directly in front of it. Unlike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
